// Digital circuit MMP-1.dig as structural Verilog
module MMP_1 (
);

  wire Addr_Dest, Addr_Src, Addr_Step, alu_1_data_ready, and_1_out, and_2_out, and_3_out, and_4_out,
       and_5_out, and_6_out, and_7_out, and_8_out, and_9_out, Clk, comparator_1_eq, comparator_2_eq,
       comparator_2_gt, comparator_2_lt, comparator_3_lt, comparator_4_eq, comparator_5_eq, counter_1_ovf,
       nClk, not_2_out, nRst, or_2_out, Out_Dev, Res_out, Rst, Step_Inc;
  wire [1:0] counter_2_out;
  wire [4:0] DispXIndex_q, multiplexer_6_out;
  wire [10:0] Addr_Match_out;
  wire [15:0] Addr, Dest, PrgmStep, Src;
  wire [15:5] multiplexer_6_out_2;
  wire [31:0] alu_1_data_out, DispCValues_q, multiplexer_1_out, multiplexer_2_out, multiplexer_3_out,
       multiplexer_4_out, multiplexer_5_out, ramdualport_1_d, rom_1_d, Temp_q;
  wire [31:16] multiplexer_6_out_3;

  Button u_Clk (.out(Clk));
  not not_1 (nClk, Clk);
  Button Res (.out(Res_out));
  Register #(.Bits(16)) u_Src (.D(multiplexer_6_out_3), .C(Clk), .en(Addr_Step), .Q(Src));
  Register #(.Bits(16)) u_Dest (.D({multiplexer_6_out_2, multiplexer_6_out}), .C(Clk), .en(Addr_Step), .Q(Dest));
  not not_2 (not_2_out, comparator_1_eq);
  and and_1 (and_1_out, not_2_out, Step_Inc);
  // Probe Clk on Clk
  RS_FF_AS rs_ff_as_1 (.S(Res_out), .R(counter_1_ovf), .Q(Rst), .nQ(nRst));
  assign Addr = Addr_Src ? Src : 16'bz;  // Driver driver_1
  assign Addr = Addr_Dest ? Dest : 16'bz;  // Driver driver_2
  Comparator #(.Bits(16)) comparator_1 (.a({16{1'b1}}), .b(Dest), .eq(comparator_1_eq));  // open: gt, lt
  CounterPreset #(.Bits(16)) Step (
    .en(and_1_out), .C(Clk), .dir(1'b0), .in({16{1'b0}}), .ld(1'b0), .clr(Rst), .out(PrgmStep));  // open: ovf
  Counter #(.Bits(2)) counter_1 (.en(Rst), .C(nClk), .clr(1'b0), .ovf(counter_1_ovf));  // open: out
  assign Addr = Addr_Step ? PrgmStep : 16'bz;  // Driver driver_3
  Register #(.Bits(32)) Temp (
    .D({multiplexer_6_out_3, multiplexer_6_out_2, multiplexer_6_out}), .C(Clk), .en(Addr_Src), .Q(Temp_q));
  Counter #(.Bits(2)) counter_2 (.en(1'b1), .C(nClk), .clr(Rst), .out(counter_2_out));  // open: ovf
  // Probe Copy Step on counter_2_out
  Decoder #(.Selector_Bits(2)) decoder_1 (
    .sel(counter_2_out), .out_0(Addr_Step), .out_1(Addr_Src), .out_2(Addr_Dest), .out_3(Step_Inc));
  Multiplexer #(.Bits(32)) multiplexer_1 (.sel(Addr_Dest), .in_0({32{1'b0}}), .in_1(Temp_q), .out(multiplexer_1_out));
  Comparator #(.Bits(16)) comparator_2 (
    .a(Addr), .b(16'h4000), .gt(comparator_2_gt), .eq(comparator_2_eq), .lt(comparator_2_lt));
  Comparator #(.Bits(16)) comparator_3 (.a(Addr), .b(16'h8000), .lt(comparator_3_lt));  // open: gt, eq
  LookUpTable #(.Bits(11)) Addr_Match (
    .in0(Addr[0]), .in1(Addr[1]), .in2(Addr[2]), .in3(Addr[3]), .in4(Addr[4]), .in5(Addr[5]), .in6(Addr[6]),
    .in7(Addr[7]), .in8(Addr[8]), .in9(Addr[9]), .in10(Addr[10]), .in11(Addr[11]), .in12(Addr[12]),
    .in13(Addr[13]), .in14(Addr[14]), .in15(Addr[15]), .out(Addr_Match_out));
  Comparator #(.Bits(6)) comparator_4 (.a(Addr[5:0]), .b({6{1'b0}}), .eq(comparator_4_eq));  // open: gt, lt
  Comparator #(.Bits(6)) comparator_5 (.a(Addr[5:0]), .b(6'b000001), .eq(comparator_5_eq));  // open: gt, lt
  or or_1 (Out_Dev, Addr_Src, Addr_Step);
  or or_2 (or_2_out, comparator_2_gt, comparator_2_eq);
  and and_2 (and_2_out, or_2_out, comparator_3_lt);
  and and_3 (and_3_out, Addr_Dest, comparator_4_eq);
  and and_4 (and_4_out, comparator_4_eq, Out_Dev);
  and and_5 (and_5_out, Addr_Dest, comparator_5_eq);
  and and_6 (and_6_out, comparator_5_eq, Out_Dev);
  // Probe Source on Src
  // Probe Destination on Dest
  and and_7 (and_7_out, Addr_Dest, and_2_out);
  and and_8 (and_8_out, and_2_out, Out_Dev);
  ALU alu_1 (
    .Ctrl_In(Addr_Dest), .Ctrl_Out(Out_Dev), .Clk(Clk),
    .Data_In({multiplexer_6_out_3, multiplexer_6_out_2, multiplexer_6_out}), .Sel_A(Addr_Match_out[0]),
    .Sel_B(Addr_Match_out[1]), .Sel_SUM(Addr_Match_out[2]), .Sel_AND(Addr_Match_out[3]),
    .Sel_OR(Addr_Match_out[4]), .Sel_XOR(Addr_Match_out[5]), .Sel_NOT(Addr_Match_out[6]),
    .Sel_GT(Addr_Match_out[7]), .Sel_GTE(Addr_Match_out[8]), .Sel_LT(Addr_Match_out[9]),
    .Sel_LTE(Addr_Match_out[10]), .Data_Out(alu_1_data_out), .Data_Ready(alu_1_data_ready));
  Register #(.Bits(5)) DispXIndex (.D(multiplexer_6_out), .C(Clk), .en(and_3_out), .Q(DispXIndex_q));
  Register #(.Bits(32)) DispCValues (
    .D({multiplexer_6_out_3, multiplexer_6_out_2, multiplexer_6_out}), .C(Clk), .en(and_5_out),
    .Q(DispCValues_q));
  LED led_1 (.in(Addr_Step));
  LED led_2 (.in(Addr_Src));
  LED led_3 (.in(Addr_Dest));
  LED led_4 (.in(Step_Inc));
  // Probe Program Step on PrgmStep
  // Probe Address on Addr
  // Probe Bus on {multiplexer_6_out_3, multiplexer_6_out_2, multiplexer_6_out}
  ROM #(.bigEndian("true"), .AddrBits(14), .Bits(32)) rom_1 (.A(Addr[13:0]), .sel(1'b1), .D(rom_1_d));
  and and_9 (and_9_out, comparator_2_lt, Out_Dev);
  RAMDualPort #(.AddrBits(14), .Bits(32)) ramdualport_1 (
    .A(Addr[13:0]), .Din({multiplexer_6_out_3, multiplexer_6_out_2, multiplexer_6_out}), .str(and_7_out),
    .C(Clk), .ld(1'b1), .D(ramdualport_1_d));
  LedMatrix #(.colAddrBits(5), .rowDataBits(32)) ledmatrix_1 (.rows(DispCValues_q), .column(DispXIndex_q));
  Multiplexer #(.Bits(32)) multiplexer_2 (
    .sel(and_9_out), .in_0(multiplexer_1_out), .in_1(rom_1_d), .out(multiplexer_2_out));
  Multiplexer #(.Bits(32)) multiplexer_3 (
    .sel(and_8_out), .in_0(multiplexer_2_out), .in_1(ramdualport_1_d), .out(multiplexer_3_out));
  Multiplexer #(.Bits(32)) multiplexer_4 (
    .sel(alu_1_data_ready), .in_0(multiplexer_3_out), .in_1(alu_1_data_out), .out(multiplexer_4_out));
  Multiplexer #(.Bits(32)) multiplexer_5 (
    .sel(and_4_out), .in_0(multiplexer_4_out), .in_1({{27{1'b0}}, DispXIndex_q}), .out(multiplexer_5_out));
  Multiplexer #(.Bits(32)) multiplexer_6 (
    .sel(and_6_out), .in_0(multiplexer_5_out), .in_1(DispCValues_q),
    .out({multiplexer_6_out_3, multiplexer_6_out_2, multiplexer_6_out}));
  // Pins of 6 and 16 bits meet at Addr
  // Pins of 6 and 16 bits meet at 16'hf100
  // Pins of 6 and 16 bits meet at 16'hf101

  // Other names for the same wires on the sheet: MemAddr[13:0] = Addr[13:0]; In_SrcDest = Addr_Step;
  //   In_Temp = Addr_Src; In_Dev = Addr_Dest; Out_Temp = Addr_Dest

  // Notes on the sheet:
  //   Control changes on -Clk
  //   Data changes on +Clk
  //   0x0000-0x3FFF : ROM
  //   0x4000-0x7FFF : RAM
  //   0xF000-0xF00A : ALU A, B,
  //   SUM, AND, OR, XOR, NOT,
  //   GT, GTE, LT, LTE
  //   0xF100 : Display X index
  //   0xF101 : Display Column values
  //   0xFFFF : Step
  //   contents of Addr_Match (hex, n*v repeats v):
  //   61440*0,1,2,4,8,e,1a,34,80,ae,14a,214
  //   Load pointers
  //   Read Source
  //   Write Destination
  //   Increment Step
  //   rom_1 loads program.bin
endmodule
